# Fritzing sketch mt1050 (saved by Fritzing 0.9.6b)
circuit board: 4.2cm x 4.9cm
perfboards: 1

parts:
  Arduino_Nano = Arduino Nano (Rev3.0)
  ULN2003a = ULN2003A [package="DIP16 [THT]"]
  J1 = male pin header, 8 pins [form="♂ (male)"]
  Screen = male pin header, 4 pins [form="♂ (male)"]
  J2 = male pin header, 4 pins [form="♂ (male)"]
  J3 = male pin header, 4 pins [form="♂ (male)"]
  J4 = male pin header, 1 pin [form="♂ (male)"]
  5v = male pin header, 7 pins [form="♂ (male)"]
  Gnd = male pin header, 7 pins [form="♂ (male)"]
  5v_2 = male pin header, 4 pins [form="♂ (male)"]
  Gnd_2 = male pin header, 4 pins [form="♂ (male)"]
  J5 = male pin header, 2 pins [form="♂ (male)"]
  5v_3 = male pin header, 4 pins [form="♂ (male)"]
  Gnd_3 = male pin header, 4 pins [form="♂ (male)"]
  J6 = male pin header, 5 pins [form="♂ (male)"]
  12V = male pin header, 13 pins [form="♂ (male)"]
  BC547b = TRANSISTOR_NPN [part_number=BC547b package=to-92-ammo]
  12V_2 = male pin header, 2 pins [form="♂ (male)"]
  SBus = male pin header, 3 pins [form="♂ (male)" part_number=SBus]
  4k7 = Resistor [tolerance=±5% power=0.25 resistance=4.7k package=THT]
  10k = Resistor [tolerance=±5% power=0.25 resistance=10k package=THT]
  12V_3 = male pin header, 4 pins [form="♂ (male)"]
  J7 = male pin header, 4 pins [form="♂ (male)"]
  J8 = male pin header, 4 pins [form="♂ (male)"]

nets:
  N1: Arduino_Nano.D0/RX, BC547b.E, 10k.Pin_1
  N2: Arduino_Nano.GND, ULN2003a.0V, Screen.pin4, Gnd.pin1, Gnd.pin2, Gnd.pin3, Gnd.pin4, Gnd.pin5, Gnd.pin6, Gnd.pin7, Gnd_2.pin1, Gnd_2.pin2, Gnd_2.pin3, Gnd_2.pin4, Gnd_3.pin1, Gnd_3.pin2, Gnd_3.pin3, Gnd_3.pin4, J6.pin1, J6.pin2, J6.pin3, J6.pin4, J6.pin5, BC547b.C, 12V_2.pin2, SBus.pin3, J7.pin1, J7.pin2, J7.pin3, J7.pin4, J8.pin1, J8.pin2, J8.pin3, J8.pin4
  N3: Arduino_Nano.D2, ULN2003a.In_7
  N4: Arduino_Nano.D3, ULN2003a.In_6
  N5: Arduino_Nano.D4, ULN2003a.In_5
  N6: Arduino_Nano.D5, ULN2003a.In_4
  N7: Arduino_Nano.D6, ULN2003a.In_3
  N8: Arduino_Nano.D7, ULN2003a.In_2
  N9: Arduino_Nano.D8, ULN2003a.In_1
  N10: Arduino_Nano.D9, J2.pin1
  N11: Arduino_Nano.D10, J2.pin2
  N12: Arduino_Nano.D11/MOSI, J2.pin3
  N13: Arduino_Nano.D12/MISO, J2.pin4
  N14: Arduino_Nano.VIN, 12V_2.pin1
  N15: Arduino_Nano.A7, J5.pin1
  N16: Arduino_Nano.A6, J5.pin2
  N17: Arduino_Nano.A5, Screen.pin2
  N18: Arduino_Nano.A4, Screen.pin1
  N19: Arduino_Nano.A3, J3.pin1
  N20: Arduino_Nano.A2, J3.pin2
  N21: Arduino_Nano.A1, J3.pin3
  N22: Arduino_Nano.A0, J3.pin4
  N23: Arduino_Nano.3V3, Screen.pin3
  N24: Arduino_Nano.D13/SCK, J4.pin1
  N25: ULN2003a.COM_-_Common, J1.pin1, 12V.pin1, 12V.pin2, 12V.pin3, 12V.pin4, 12V.pin5, 12V.pin6, 12V.pin7, 12V.pin8, 12V.pin9, 12V.pin10, 12V.pin11, 12V.pin12, 12V.pin13, 12V_3.pin1, 12V_3.pin2, 12V_3.pin3, 12V_3.pin4
  N26: ULN2003a.Out_7, J1.pin2
  N27: ULN2003a.Out_6, J1.pin3
  N28: ULN2003a.Out_5, J1.pin4
  N29: ULN2003a.Out_4, J1.pin5
  N30: ULN2003a.Out_3, J1.pin6
  N31: ULN2003a.Out_2, J1.pin7
  N32: ULN2003a.Out_1, J1.pin8
  N33: 5v.pin1, 5v.pin2, 5v.pin3, 5v.pin4, 5v.pin5, 5v.pin6, 5v.pin7, 5v_2.pin1, 5v_2.pin2, 5v_2.pin3, 5v_2.pin4, 5v_3.pin1, 5v_3.pin2, 5v_3.pin3, 5v_3.pin4
  N34: BC547b.B, 4k7.Pin_1
  N35: SBus.pin1, 4k7.Pin_0
  N36: SBus.pin2, 10k.Pin_0
